# Fritzing sketch SETUP_MACHINE_1 (saved by Fritzing 0.9.3b)
breadboards: 1

parts:
  Bauteil1 = Arduino Uno (Rev3) - ICSP
  Bauteil2 = Soil Moisture Sensor
  J1 = Basic Servo
  S1 = Round Pushbutton
  J2 = Basic Servo

nets:
  N1: Bauteil1.A0, Bauteil2.SIG
  N2: Bauteil1.ICSP_MISO, Bauteil1.D12/MISO, J2.pulse
  VCC: Bauteil1.5V, Bauteil1.D9_PWM, Bauteil2.VCC, S1.leg0, J2.vcc
  GND: Bauteil1.GND, Bauteil2.GND, J1.gnd, S1.leg1
  N3: Bauteil1.D10_PWM/SS, J1.pulse

// code stored in the sketch: Moisture_Sensor.ino
/*
Zuerst wird der servo1 attached und auf 180 grad gestellt (servo1.write(180)). Er bleitb in dieser Position bis der Button ihn ausloest. 
Wenn der Button aktiviert wird - pin 9 - also eine 1 anzeigt anstatt normalerweise einer 0 --> if (digitalRead(9) == 1)
wird der servo1 - pin 12 - von den 180 grad zurueck auf 10 grad gestellt. 
Deshalb servo1.wirte(10).

Dann passiert nichts bis der Moisture Sensor - pin A0 - einen Ausschlag ueber 200 angibt. --> if(analogRead(A0)>200).
Sobald der Ausschlag groesser als 200 ist, wird der servo2 attached und auf 10 grad gestellt. --> servo2.write(10).
Da der zweite Servo ein Continuous-Servo ist, heissen diese 10 grad, dass er sich im Uhrzeiger dreht, 
bis ihm der Strom gekappt wird. 
Ist der Ausschlag des Moisture Sensors unter 200 bleibt der servo2 detached. --> else {servo2.detach()}

*/

#include <Servo.h>
Servo servo2;
Servo servo1;

void setup() {
  pinMode(9, INPUT);
  pinMode(6, OUTPUT);
  pinMode(A0, INPUT);
  Serial.begin(9600);

    servo1.attach(12);
    servo1.write(180);

}

void loop() {

if(digitalRead(9) == 1){
  servo1.attach(12);
  servo1.write(10);
  }
  else{
    //servo1.detach();
    }


if (analogRead(A0) > 200){
  servo2.attach(10);
  servo2.write(10);
  }
  else{
    servo2.detach();
    }
  
Serial.println(analogRead(A0));

  delay(1);

}
