# Fritzing sketch UltraSonicShiftLEDSketch (saved by Fritzing 0.9.3b)

parts:
  Bauteil1 = Arduino Uno (Rev3) - ICSP
  U1 = PCF8574 [package="DIP16 [THT]"]
  U2 = PCF8574 [package="DIP16 [THT]"]
  U3 = PCF8574 [package="DIP16 [THT]"]
  hc-sr1 = hc-sr04

nets:
  N1: Bauteil1.D8, U1.P7
  N2: Bauteil1.D11_PWM/MOSI, U1.SCL
  N3: Bauteil1.D12/MISO, U1.P6
  N4: Bauteil1.D13/SCK, hc-sr1.Echo
  N5: U1.P4, U2.SCL
  N6: U2.P4, U3.SCL

// code stored in the sketch: Untitled.ino
#include <ShiftOutX.h>
#include <ShiftPinNo.h>

shiftOutX regOne(8, 11, 12, MSBFIRST, 3);
 
void setup() {
 Serial.begin(9600);
}
 
void loop() {  
  long duration, cm;

  pinMode(13, OUTPUT);
  digitalWrite(13, LOW);
  delayMicroseconds(2);
  digitalWrite(13, HIGH);
  delayMicroseconds(5);
  digitalWrite(13, LOW);
  
  pinMode(13, INPUT);
  duration = pulseIn(13, HIGH);
  cm = duration / 29 / 2;
  Serial.print(cm);
  Serial.print("cm");
  Serial.println();
  regOne.allOff();
if(cm >= 70 && cm<= 80){
    regOne.pinOn(shPin1);
  }else if(cm >= 67.5){
    regOne.pinOn(shPin2);
  }else if(cm >= 65){
    regOne.pinOn(shPin3);
  }else if(cm >= 62.5){
    regOne.pinOn(shPin4);
  }else if(cm >= 60){
    regOne.pinOn(shPin5);
  }else if(cm >= 57.5){
    regOne.pinOn(shPin6);
  }else if(cm >= 55){
    regOne.pinOn(shPin7);
  }else if(cm >= 52.5){
    regOne.pinOn(shPin8);
  }else if(cm >= 50){
    regOne.pinOn(shPin9);
  }else if(cm >= 47.5){
    regOne.pinOn(shPin10);
  }else if(cm >= 45){
    regOne.pinOn(shPin11);
  }else if(cm >= 42.5){
    regOne.pinOn(shPin12);
  }else if(cm >= 40){
    regOne.pinOn(shPin13);
  }else if(cm >= 35){
    regOne.pinOn(shPin14);
  }else if(cm >= 32.5){
    regOne.pinOn(shPin15);
  }else if(cm >= 30){
    regOne.pinOn(shPin16);
  }else if(cm >= 27.5){
    regOne.pinOn(shPin17);
  }else if(cm >= 25){
    regOne.pinOn(shPin18);
  }else if(cm >= 22.5){
    regOne.pinOn(shPin18);
  }else if(cm >= 20){
    regOne.pinOn(shPin19);
  }else if(cm >= 17.5){
    regOne.pinOn(shPin20);
  }else if(cm >= 15){
    regOne.pinOn(shPin21);
  }else if(cm >= 13.5){
    regOne.pinOn(shPin22);
  }else if(cm >= 11.5){
    regOne.pinOn(shPin23);
  }else if(cm >= 10){
    regOne.pinOn(shPin24);
  }
  delay(100);
}
