# Fritzing sketch Modulesetup (saved by Fritzing 0.9.3b)
breadboards: 1

parts:
  LED2 = smd LED [color="Red (633nm)" package="0805 [SMD]"]
  Bauteil1 = Arduino Uno (Rev3) - ICSP
  Q1 = Basic FET P-Channel [package="TO220 [THT]"]
  R1 = Resistor [tolerance=±5% resistance=220 package=THT]
  T1 = LM35 Temperature Sensor [package="TO92 [THT]"]
  LED1 = smd LED [color="Red (633nm)" package="0805 [SMD]"]
  U1 = RELAY [package=relay-g5q]
  J1 = Piezo Speaker
  D1 = Diode [package=diode-1n4148]
  J2 = Basic Servo

nets:
  GND: LED2.cathode, Bauteil1.GND, T1.GND, LED1.cathode, U1.COIL2, J1.pin1, J2.gnd
  N1: LED2.anode, Q1.drain, LED1.anode, D1.A
  N2: Bauteil1.A0, T1.Vout
  N3: Bauteil1.D8, U1.COIL1
  N4: Bauteil1.D13/SCK, R1.Pin_1
  N5: Bauteil1.D1/TX, J2.pulse
  5V: Bauteil1.5V, Q1.gate, T1.+Vs, U1.MAIN, D1.C, J2.vcc
  N6: Q1.source, R1.Pin_0
  N7: U1.NO, J1.pin2
