# Fritzing sketch Relais (saved by Fritzing 0.9.3b)

parts:
  Bauteil1 = Arduino Uno (Rev3)  # not connected
  M1 = DC Motor
  U1 = LIPO-1000mAh [package=lipo-1000]

nets:
  N1: M1.pin_2, U1.-

// code stored in the sketch: Untitled.ino
void setup() {
  pinMode(12,OUTPUT);
}

void loop() {
    digitalWrite(12,HIGH);
  delay(100);
}
